// Logisim project Project2Given.circ as structural Verilog: 4 circuits, main circuit main
module main (
);

  wire and_1_out, and_2_out, B0, B1, B2, B3, B4, B5, B6, B7, B8, B9, BL, BU, C0, C1, C2, CLK, lock_1_l,
       lock_1_u, not_1_out, or_8_out, P1_v, R0, R1, R3, R4, Valid;
  wire [2:0] counter_1_q;
  wire [3:0] IB_out_7, P1_b0, register_3_q, register_4_q, register_5_q;

  Button n1 (.out(B1));
  Button n4 (.out(B4));
  Button n7 (.out(B7));
  Button L (.out(BL));
  Button n3 (.out(B3));
  Button n2 (.out(B2));
  Button n6 (.out(B6));
  Button n5 (.out(B5));
  Button n9 (.out(B9));
  Button n8 (.out(B8));
  Button U (.out(BU));
  Button n0 (.out(B0));
  or or_1 (R0, B3, B2, B1);
  or or_2 (R1, B6, B5, B4);
  or or_3 (R3, B9, B8, B7);
  or or_4 (R4, BU, B0, BL);
  or or_5 (C0, B1, B4, B7, BL);
  or or_6 (C1, B2, B5, B8, B0);
  or or_7 (C2, B3, B6, B9, BU);
  Clock clock_1 (.out(CLK));
  nand nand_1 (Valid, IB_out_7[0], IB_out_7[1], IB_out_7[2], IB_out_7[3]);
  // Probe on P1_b0
  Panel P1 (
    .R0(R0), .R1(R1), .R2(R3), .R3(R4), .C0(C0), .C1(C1), .C2(C2), .B0(P1_b0[0]), .B1(P1_b0[1]),
    .B2(P1_b0[2]), .B3(P1_b0[3]), .V(P1_v));
  LED Press (.in(P1_v));
  // Probe on IB_out_7
  InputBuffer IB (
    .in_1(P1_b0[0]), .in_2(P1_b0[1]), .in_3(P1_b0[2]), .in_4(P1_b0[3]), .in_5(P1_v), .in_6(not_1_out),
    .out_7(IB_out_7[0]), .out_8(IB_out_7[1]), .out_9(IB_out_7[2]), .out_10(IB_out_7[3]));
  not not_1 (not_1_out, CLK);
  Register #(.width(4)) register_1 (.D(register_3_q), .en(Valid), .clk(CLK));  // open: Q, clr
  Lock lock_1 (
    .C0(IB_out_7[0]), .C1(IB_out_7[1]), .C2(IB_out_7[2]), .C3(IB_out_7[3]), .CLK(CLK), .L(lock_1_l),
    .U(lock_1_u));
  Counter #(.max('h7), .width(3)) counter_1 (
    .count(or_8_out), .Q(counter_1_q), .up(lock_1_u), .clk(CLK));  // open: load, D, carry, clr
  or or_8 (or_8_out, lock_1_l, lock_1_u);
  Register #(.width(4)) register_2 (.D(register_3_q), .en(Valid), .clk(CLK));  // open: Q, clr
  LED Unlocked (.in(and_1_out));
  and and_1 (and_1_out, ~counter_1_q[0], ~counter_1_q[1], ~counter_1_q[2]);  // AND_Gate
  Register #(.width(4)) register_3 (.D(register_4_q), .en(Valid), .clk(CLK), .Q(register_3_q));  // open: clr
  LED Locked (.in(and_2_out));
  and and_2 (and_2_out, ~counter_1_q[0], ~counter_1_q[1], counter_1_q[2]);  // AND_Gate
  Register #(.width(4)) register_4 (.D(register_5_q), .en(Valid), .clk(CLK), .Q(register_4_q));  // open: clr
  Register #(.width(4)) register_5 (.D(IB_out_7), .en(Valid), .clk(CLK), .Q(register_5_q));  // open: clr
endmodule

module Panel (
  input  R0,
  input  R1,
  input  R2,
  input  R3,
  input  C0,
  input  C1,
  input  C2,
  output B0,
  output B1,
  output B2,
  output B3,
  output V
);

  wire and_1_out, and_2_out, and_3_out, and_4_out, and_5_out, and_6_out, and_7_out, and_9_out, and_10_out,
       and_11_out, and_12_out, and_13_out, and_14_out, and_15_out, and_16_out, and_17_out, and_18_out,
       xor_1_out, xor_2_out;

  and and_1 (and_1_out, R2, C0);
  or or_1 (B2, and_1_out, R1);
  and and_2 (and_2_out, R0, C0);
  and and_3 (and_3_out, R0, C2);
  and and_4 (and_4_out, R1, C1);
  and and_5 (and_5_out, R2, C0);
  and and_6 (and_6_out, R2, C2);
  and and_7 (and_7_out, C2, R3);
  or or_2 (B0, and_2_out, and_3_out, and_4_out, and_5_out, and_6_out, and_7_out);
  ExactlyOne xor_1 (.out(xor_1_out), .in0(R0), .in1(R1), .in2(R2), .in3(R3));
  and and_8 (V, xor_1_out, xor_2_out);
  ExactlyOne xor_2 (.out(xor_2_out), .in0(C0), .in1(C1), .in2(C2));
  and and_9 (and_9_out, R2, C1);
  and and_10 (and_10_out, R2, C2);
  and and_11 (and_11_out, R3, C0);
  and and_12 (and_12_out, R3, C2);
  or or_3 (B3, and_9_out, and_10_out, and_11_out, and_12_out);
  and and_13 (and_13_out, R0, C1);
  and and_14 (and_14_out, R0, C2);
  or or_4 (B1, and_13_out, and_14_out, and_15_out, and_16_out, and_17_out, and_18_out);
  and and_15 (and_15_out, R1, C2);
  and and_16 (and_16_out, R2, C0);
  and and_17 (and_17_out, R3, C0);
  and and_18 (and_18_out, R3, C2);
endmodule

module InputBuffer (
  input  in_1,
  input  in_2,
  input  in_3,
  input  in_4,
  input  in_5,
  input  in_6,
  output out_7,
  output out_8,
  output out_9,
  output out_10
);

  wire and_1_out, and_2_out, CLK, clock_1_out, multiplexer_1_out, multiplexer_2_out, multiplexer_3_out,
       multiplexer_4_out, or_2_out, Vout, X_q, X_qn, Y_q, Y_qn;

  or or_1 (CLK, clock_1_out, in_6);
  Clock clock_1 (.out(clock_1_out));
  and and_1 (and_1_out, X_q, in_5);
  D_Flip_Flop X (.D(or_2_out), .clk(CLK), .Q(X_q), .Qn(X_qn));  // open: preset, reset
  or or_2 (or_2_out, and_1_out, Y_q);
  D_Flip_Flop Y (.D(and_2_out), .clk(CLK), .Q(Y_q), .Qn(Y_qn));  // open: preset, reset
  and and_2 (and_2_out, in_5, X_qn, Y_qn);
  and and_3 (Vout, X_qn, Y_q);
  D_Flip_Flop d_ff_1 (.D(multiplexer_1_out), .clk(CLK), .Q(out_7));  // open: Qn, preset, reset
  Multiplexer multiplexer_1 (.in0(1'b1), .in1(in_1), .out(multiplexer_1_out), .sel(Vout));
  D_Flip_Flop d_ff_2 (.D(multiplexer_2_out), .clk(CLK), .Q(out_8));  // open: Qn, preset, reset
  Multiplexer multiplexer_2 (.in0(1'b1), .in1(in_2), .out(multiplexer_2_out), .sel(Vout));
  D_Flip_Flop d_ff_3 (.D(multiplexer_3_out), .clk(CLK), .Q(out_9));  // open: Qn, preset, reset
  Multiplexer multiplexer_3 (.in0(1'b1), .in1(in_3), .out(multiplexer_3_out), .sel(Vout));
  D_Flip_Flop d_ff_4 (.D(multiplexer_4_out), .clk(CLK), .Q(out_10));  // open: Qn, preset, reset
  Multiplexer multiplexer_4 (.in0(1'b1), .in1(in_4), .out(multiplexer_4_out), .sel(Vout));

  // Other names for the same wires on the sheet: B0 = in_1; B1 = in_2; B2 = in_3; B3 = in_4; C0 = out_7; C1 = out_8;
  //   C2 = out_9; C3 = out_10; V = in_5
endmodule

module Lock (
  input  C0,
  input  C1,
  input  C2,
  input  C3,
  input  CLK,
  output L,
  output U
);

  wire and_2_out, and_7_out, and_8_out, and_9_out, and_10_out, and_11_out, and_12_out, and_13_out,
       and_14_out, and_15_out, and_16_out, and_17_out, and_18_out, and_19_out, and_20_out, and_21_out,
       and_22_out, and_25_out, and_26_out, and_27_out, and_28_out, and_29_out, and_30_out, and_31_out,
       and_32_out, and_33_out, and_34_out, Buff, D, d_ff_1_qn, d_ff_2_q, d_ff_2_qn, d_ff_3_q, d_ff_3_qn,
       d_ff_4_q, d_ff_4_qn, d_ff_5_q, d_ff_5_qn, LDigit, LOCKED, Lpress, Lstart, LValid, lX_q, lX_qn, lY_q,
       lY_qn, lZ_q, lZ_qn, mX_q, mX_qn, mY_q, mY_qn, nand_1_out, nand_2_out, or_3_out, or_4_out, or_5_out,
       or_6_out, or_8_out, or_10_out, or_11_out, or_12_out, or_13_out, or_16_out, Ucheck, UDigit, Umatch,
       UNLOCKED, Upress, Ustart, UValid, xnor_1_out, xnor_2_out, xnor_3_out, xnor_4_out, xnor_5_out,
       xnor_6_out, xnor_7_out, xnor_8_out, xnor_9_out, xnor_10_out, xnor_11_out, xnor_12_out;
  wire [1:0] W;
  wire [2:0] counter_1_q;
  wire [3:0] register_1_q, register_2_q;
  wire [7:0] register_5_q, register_6_q;

  and and_1 (Buff, C0, C1, C2, C3);
  and and_2 (and_2_out, Lpress, ~Upress);  // AND_Gate
  and and_3 (Lpress, ~C0, C1, ~C2, C3);  // AND_Gate
  and and_4 (Upress, C0, C1, ~C2, C3);  // AND_Gate
  nor nor_1 (D, Lpress, Buff, Upress);
  or or_1 (W[0], Buff, and_2_out);
  or or_2 (W[1], D, Buff);
  nand nand_1 (nand_1_out, C0, C1, C2, C3);
  and and_5 (LValid, nand_1_out, D, LDigit);
  nand nand_2 (nand_2_out, C0, C1, C2, C3);
  and and_6 (UValid, nand_2_out, D, UDigit);
  and and_7 (and_7_out, W[1], d_ff_3_q, ~W[0], d_ff_2_q, d_ff_1_qn);  // AND_Gate
  and and_8 (and_8_out, d_ff_1_qn, W[1], ~W[0], d_ff_3_q, d_ff_2_qn);  // AND_Gate
  and and_9 (and_9_out, d_ff_1_qn, W[1], W[0], ~d_ff_3_qn);  // AND_Gate
  and and_10 (and_10_out, lX_qn, lY_q, W[1], ~W[0], lZ_qn);  // AND_Gate
  and and_11 (and_11_out, d_ff_2_q, d_ff_1_qn, W[1], d_ff_3_qn);
  and and_12 (and_12_out, d_ff_1_qn, ~W[0], ~W[1]);  // AND_Gate
  and and_13 (and_13_out, lY_qn, ~W[1], W[0], lZ_qn);  // AND_Gate
  and and_14 (and_14_out, d_ff_1_qn, W[0], W[1], ~d_ff_2_qn);  // AND_Gate
  and and_15 (and_15_out, d_ff_2_q, W[1], ~W[0], d_ff_3_qn);  // AND_Gate
  and and_16 (and_16_out, ~lX_q, lZ_q, ~W[1], lY_qn, W[0]);  // AND_Gate
  and and_17 (and_17_out, W[1], lZ_q, ~W[0], lY_q, lX_qn);  // AND_Gate
  and and_18 (and_18_out, lY_q, lZ_qn, W[1]);
  and and_19 (and_19_out, lY_q, W[0], W[1]);
  and and_20 (and_20_out, lX_qn, W[1], ~W[0], lZ_q, lY_qn);  // AND_Gate
  and and_21 (and_21_out, lX_qn, lZ_q, W[1], W[0]);
  and and_22 (and_22_out, W[0], lY_qn, lX_qn, ~W[1]);  // AND_Gate
  D_Flip_Flop d_ff_1 (.D(and_7_out), .clk(CLK), .Q(Ucheck), .Qn(d_ff_1_qn));  // open: preset, reset
  D_Flip_Flop d_ff_2 (.D(or_3_out), .clk(CLK), .Q(d_ff_2_q), .Qn(d_ff_2_qn));  // open: preset, reset
  or or_3 (or_3_out, and_11_out, and_8_out, and_14_out);
  D_Flip_Flop d_ff_3 (.D(or_4_out), .clk(CLK), .Q(d_ff_3_q), .Qn(d_ff_3_qn));  // open: preset, reset
  or or_4 (or_4_out, and_12_out, and_9_out, and_15_out);
  or or_5 (or_5_out, and_16_out, and_17_out);
  or or_6 (or_6_out, and_18_out, and_19_out, and_20_out);
  or or_7 (UDigit, d_ff_2_q, d_ff_3_q);
  Register #(.width(4)) register_1 (.D({C3, C2, C1, C0}), .en(LValid), .clk(CLK), .Q(register_1_q));  // open: clr
  Register #(.width(4)) register_2 (.D({C3, C2, C1, C0}), .en(UValid), .clk(CLK), .Q(register_2_q));  // open: clr
  D_Flip_Flop lX (.D(or_5_out), .clk(CLK), .Q(lX_q), .Qn(lX_qn));  // open: preset, reset
  D_Flip_Flop lY (.D(or_6_out), .clk(CLK), .Q(lY_q), .Qn(lY_qn));  // open: preset, reset
  D_Flip_Flop lZ (.D(or_8_out), .clk(CLK), .Q(lZ_q), .Qn(lZ_qn));  // open: preset, reset
  or or_8 (or_8_out, and_21_out, and_22_out, and_13_out, and_10_out);
  and and_23 (Ustart, Ucheck, Umatch, LOCKED);
  or or_9 (LDigit, lY_q, lZ_q);
  Register #(.width(4)) register_3 (.D(register_1_q), .en(LValid), .clk(CLK), .Q(register_5_q[7:4]));  // open: clr
  Register #(.width(4)) register_4 (.D(register_2_q), .en(UValid), .clk(CLK), .Q(register_6_q[7:4]));  // open: clr
  and and_24 (Lstart, lX_q, UNLOCKED);
  Register #(.width(4)) register_5 (.D(register_5_q[7:4]), .en(LValid), .clk(CLK), .Q(register_5_q[3:0]));  // open: clr
  Register #(.width(4)) register_6 (.D(register_6_q[7:4]), .en(UValid), .clk(CLK), .Q(register_6_q[3:0]));  // open: clr
  and and_25 (and_25_out, d_ff_5_q, d_ff_4_qn);
  D_Flip_Flop mX (.D(or_10_out), .clk(CLK), .Q(mX_q), .Qn(mX_qn));  // open: preset, reset
  and and_26 (and_26_out, mY_q, mX_qn);
  or or_10 (or_10_out, and_26_out, and_27_out);
  and and_27 (and_27_out, mY_qn, mX_q);
  D_Flip_Flop mY (.D(or_11_out), .clk(CLK), .Q(mY_q), .Qn(mY_qn));  // open: preset, reset
  and and_28 (and_28_out, mX_q, mY_qn);
  or or_11 (or_11_out, and_28_out, and_29_out);
  and and_29 (and_29_out, mY_qn, mX_qn, Lstart);
  D_Flip_Flop d_ff_4 (.D(or_12_out), .clk(CLK), .Q(d_ff_4_q), .Qn(d_ff_4_qn));  // open: preset, reset
  or or_12 (or_12_out, and_25_out, and_30_out);
  and and_30 (and_30_out, d_ff_5_qn, d_ff_4_q);
  D_Flip_Flop d_ff_5 (.D(or_13_out), .clk(CLK), .Q(d_ff_5_q), .Qn(d_ff_5_qn));  // open: preset, reset
  and and_31 (and_31_out, d_ff_4_q, d_ff_5_qn);
  or or_13 (or_13_out, and_31_out, and_32_out);
  and and_32 (and_32_out, d_ff_5_qn, d_ff_4_qn, Ustart);
  and and_33 (and_33_out, mX_qn, Lstart);
  or or_14 (U, d_ff_4_q, d_ff_5_q, and_34_out);
  and and_34 (and_34_out, d_ff_4_qn, Ustart);
  or or_15 (L, mX_q, mY_q, and_33_out);
  xnor xnor_1 (xnor_1_out, register_5_q[0], register_6_q[0]);
  xnor xnor_2 (xnor_2_out, register_5_q[1], register_6_q[1]);
  xnor xnor_3 (xnor_3_out, register_5_q[2], register_6_q[2]);
  xnor xnor_4 (xnor_4_out, register_5_q[3], register_6_q[3]);
  xnor xnor_5 (xnor_5_out, register_5_q[4], register_6_q[4]);
  xnor xnor_6 (xnor_6_out, register_5_q[5], register_6_q[5]);
  xnor xnor_7 (xnor_7_out, register_5_q[6], register_6_q[6]);
  xnor xnor_8 (xnor_8_out, register_5_q[7], register_6_q[7]);
  xnor xnor_9 (xnor_9_out, register_1_q[0], register_2_q[0]);
  xnor xnor_10 (xnor_10_out, register_1_q[1], register_2_q[1]);
  xnor xnor_11 (xnor_11_out, register_2_q[2], register_1_q[2]);
  xnor xnor_12 (xnor_12_out, register_2_q[3], register_1_q[3]);
  and and_35 (Umatch, xnor_1_out, xnor_2_out, xnor_3_out, xnor_4_out, xnor_5_out, xnor_6_out, xnor_7_out, xnor_8_out, xnor_9_out, xnor_10_out, xnor_11_out, xnor_12_out);
  or or_16 (or_16_out, L, U);
  Counter #(.max('h7), .width(3)) counter_1 (
    .count(or_16_out), .Q(counter_1_q), .up(U), .clk(CLK));  // open: load, D, carry, clr
  and and_36 (UNLOCKED, ~counter_1_q[0], ~counter_1_q[1], ~counter_1_q[2]);  // AND_Gate
  and and_37 (LOCKED, ~counter_1_q[0], ~counter_1_q[1], counter_1_q[2]);  // AND_Gate

  // Other names for the same wires on the sheet: LOCKING = L; UNLOCKING = U
endmodule
